# Fritzing sketch 3_1 (saved by Fritzing 0.9.4)
breadboards: 1

parts:
  Part1 = Arduino Uno (Rev3)
  S1 = Pushbutton [package="[THT]"]
  part = Trimmer Potentiometer [maximum_resistance=10kΩ package=THT]
  R4 = Trimmer Potentiometer [maximum_resistance=10kΩ package=THT]
  C1 = Electrolytic Capacitor [capacitance=1µF package="100 mil [THT, electrolytic]"]

nets:
  N1: Part1.A0, part.leg2, C1.-
  N2: Part1.A1, R4.wiper
  N3: Part1.D11_PWM/MOSI, part.wiper
  N4: Part1.D2, S1.Pin_1, S1.Pin_2
  N5: Part1.5V, R4.leg2
  N6: Part1.GND, S1.Pin_3, S1.Pin_4, R4.leg1, C1.+
