# Fritzing sketch 3_2 (saved by Fritzing 0.9.4)
breadboards: 1

parts:
  R2 = Trimmer Potentiometer [maximum_resistance=10kΩ package=THT]
  C1 = Electrolytic Capacitor [capacitance=1µF package="100 mil [THT, electrolytic]"]
  Part1 = Arduino Uno (Rev3)

nets:
  N1: R2.wiper, Part1.D10_PWM/SS
  N2: R2.leg2, C1.-, Part1.A1
  N3: C1.+, Part1.GND
