# Fritzing sketch Untitled Sketch (saved by Fritzing 0.9.4)
breadboards: 1

parts:
  U2 = LM124-324 Quad Opamp [package="DIP (Dual Inline)"]
  part = Arduino Uno (Rev3)
  part_2 = Temperature Sensor (Thermistor) [thermistor_type=NTC package=THT]
  part_3 = Resistor [tolerance=±5% resistance=10k package=THT]
  part_4 = Resistor [tolerance=±5% resistance=10k package=THT]
  part_5 = Resistor [tolerance=±5% resistance=33k package=THT]
  part_6 = Resistor [tolerance=±5% resistance=100k package=THT]
  part_7 = Resistor [tolerance=±5% resistance=100k package=THT]
  part_8 = Resistor [tolerance=±5% resistance=100k package=THT]
  part_9 = Resistor [tolerance=±5% resistance=100k package=THT]
  R4 = Trimmer Potentiometer [maximum_resistance=10kΩ package=THT]

nets:
  N1: U2.1OUT, part.A0, part_9.Pin_1
  N2: U2.1IN-, part_8.Pin_0, part_9.Pin_0
  N3: U2.1IN+, part_6.Pin_1, part_7.Pin_0
  N4: U2.VCC+, part.5V
  N5: U2.VCC-, part.GND
  N6: part.AREF, R4.wiper
  GND: part_2.pin_0, part_5.Pin_0, part_7.Pin_1, R4.leg1
  N7: part_2.pin_1, part_3.Pin_0, part_8.Pin_1
  5V: part_3.Pin_1, part_4.Pin_0, R4.leg2
  N8: part_4.Pin_1, part_5.Pin_1, part_6.Pin_0
